# Fritzing sketch hookup (saved by Fritzing 1.0.3b)
breadboards: 1

parts:
  OLED_I2C1 = OLED 128x64 I2C Monochrome Display
  Part1 = SPI OLED Monochrome 128x64 0.96 inch
  J1 = shrouded pin header, 40 pins [form="♂ (shrouded male)"]

nets:
  N1: OLED_I2C1.SDA, J1.pin34
  N2: OLED_I2C1.SCK, J1.pin7
  VDD: OLED_I2C1.VDD, Part1.VDD, J1.pin21
  GND: OLED_I2C1.GND, Part1.GND, J1.pin18
  N3: Part1.SCK, J1.pin32
  N4: Part1.SDA, J1.pin30
  N5: Part1.RES, J1.pin36
  N6: Part1.DC, J1.pin35
  N7: Part1.CS, J1.pin9

notes:
  1
  40
  2
  39
  Jetson header
  SPI
  I2C

custom parts:
  SPI OLED Monochrome 128x64 0.96 inch: Unknown 128x64 0.96 inch 128x64 SPI Monochrome OLED display
